// Logisim project Dual 7 Segment Decoder Copy.circ as structural Verilog: 13 circuits, main circuit DUAL 7 SEGMENT DECODER DESIGN 1
module DUAL_7_SEGMENT_DECODER_DESIGN_1 (
  input  C,
  input  S3,
  input  S2,
  input  S1,
  input  S0,
  output G0,
  output G1,
  output F1,
  output E1,
  output F0,
  output D1,
  output C1,
  output B1,
  output A1,
  output E0,
  output D0,
  output C0,
  output B0,
  output A0
);

  wire and_1_out, and_2_out, and_3_out, and_4_out, and_5_out, and_6_out, and_7_out, and_8_out, and_9_out,
       and_10_out, and_11_out, and_12_out, and_13_out, and_14_out, and_15_out, and_16_out, and_17_out,
       and_18_out, and_19_out, and_20_out, and_21_out, and_22_out, and_23_out, and_24_out, and_25_out,
       and_26_out, and_27_out, and_28_out, and_29_out, and_30_out, and_31_out, and_32_out, and_33_out,
       and_34_out, and_35_out, and_36_out, and_37_out, and_38_out, and_39_out, and_40_out, and_41_out,
       and_42_out, and_43_out, and_44_out, and_45_out, and_46_out, and_47_out, and_48_out, and_49_out,
       and_50_out, and_51_out, and_52_out, and_53_out, and_54_out, and_55_out, and_56_out, and_57_out,
       and_58_out, and_59_out, and_60_out, and_61_out, and_62_out, and_63_out, and_64_out, and_65_out,
       and_66_out, and_67_out, and_68_out, and_69_out, and_70_out, C_prime, S0_prime, S1_prime, S2_prime,
       S3_prime;

  not not_1 (C_prime, C);
  Pull_Resistor pull_resistor_1 (.node(C));
  not not_2 (S3_prime, S3);
  not not_3 (S2_prime, S2);
  not not_4 (S1_prime, S1);
  and and_1 (and_1_out, C, S2);
  and and_2 (and_2_out, C, S3);
  and and_3 (and_3_out, C_prime, S3_prime);
  and and_4 (and_4_out, C_prime, S2_prime, S1_prime);
  and and_5 (and_5_out, S3_prime, S2);
  and and_6 (and_6_out, C, S3, S2_prime);
  and and_7 (and_7_out, C_prime, S2_prime, S1_prime);
  and and_8 (and_8_out, C, S2, S1_prime);
  and and_9 (and_9_out, C_prime, S3_prime);
  and and_10 (and_10_out, C, S3);
  and and_11 (and_11_out, C_prime, S2_prime, S1_prime);
  and and_12 (and_12_out, S3_prime, S2);
  and and_13 (and_13_out, S3_prime, S2_prime);
  and and_14 (and_14_out, S3, S2, S1);
  and and_15 (and_15_out, C_prime, S3_prime);
  and and_16 (and_16_out, C, S3);
  and and_17 (and_17_out, C_prime, S2_prime, S1_prime);
  and and_18 (and_18_out, S3_prime, S2);
  not not_5 (S0_prime, S0);
  or or_1 (G1, and_1_out, and_2_out);
  or or_2 (F1, and_3_out, and_4_out);
  or or_3 (E1, and_3_out, and_5_out, and_6_out, and_7_out, and_8_out);
  or or_4 (D1, and_9_out, and_10_out, and_11_out, and_12_out);
  or or_5 (C1, C_prime, and_13_out, and_14_out);
  or or_6 (A1, and_15_out, and_16_out, and_17_out, and_18_out);
  and and_19 (and_19_out, S3_prime, S2_prime, S1);
  and and_20 (and_20_out, C_prime, S2, S1_prime);
  and and_21 (and_21_out, S3, S1_prime);
  and and_22 (and_22_out, C_prime, S3, S2);
  and and_23 (and_23_out, C, S2_prime, S0_prime);
  and and_24 (and_24_out, C, S3_prime, S1);
  and and_25 (and_25_out, S3_prime, S1, S0_prime);
  and and_26 (and_26_out, C_prime, S3_prime, S2, S1_prime);
  and and_27 (and_27_out, S3, S2_prime, S1_prime);
  and and_28 (and_28_out, C_prime, S3, S2, S1);
  and and_29 (and_29_out, C, S3_prime, S2_prime, S1);
  and and_30 (and_30_out, C, S3, S1_prime);
  and and_31 (and_31_out, S3_prime, S1_prime, S0_prime);
  and and_32 (and_32_out, C_prime, S3_prime, S2, S0_prime);
  and and_33 (and_33_out, S3, S1, S0_prime);
  and and_34 (and_34_out, S3_prime, S1, S0_prime);
  and and_35 (and_35_out, C_prime, S2_prime, S0_prime);
  and and_36 (and_36_out, S3, S2, S1_prime, S0_prime);
  and and_37 (and_37_out, C, S3_prime, S0_prime);
  and and_38 (and_38_out, C, S1, S0_prime);
  and and_39 (and_39_out, C_prime, S3_prime, S2_prime, S1);
  and and_40 (and_40_out, C_prime, S2, S1_prime, S0);
  and and_41 (and_41_out, S3_prime, S1, S0_prime);
  and and_42 (and_42_out, C_prime, S3, S2, S0);
  and and_43 (and_43_out, C, S3_prime, S2, S1);
  and and_44 (and_44_out, C, S3, S2_prime, S1_prime, S0);
  and and_45 (and_45_out, C_prime, S2_prime, S0_prime);
  and and_46 (and_46_out, S3, S2, S1_prime, S0_prime);
  and and_47 (and_47_out, C, S3_prime, S0_prime);
  and and_48 (and_48_out, C, S1, S0_prime);
  and and_49 (and_49_out, C, S2_prime);
  and and_50 (and_50_out, S3_prime, S1_prime);
  and and_51 (and_51_out, C_prime, S2, S1);
  and and_52 (and_52_out, S3, S2_prime);
  and and_53 (and_53_out, C, S3);
  and and_54 (and_54_out, S3_prime, S1, S0);
  and and_55 (and_55_out, S3, S1_prime, S0_prime);
  and and_56 (and_56_out, C_prime, S1_prime, S0_prime);
  and and_57 (and_57_out, S3_prime, S2_prime, S0);
  and and_58 (and_58_out, S3_prime, S2_prime, S1);
  and and_59 (and_59_out, C_prime, S3, S1_prime);
  and and_60 (and_60_out, C_prime, S3, S0_prime);
  and and_61 (and_61_out, S2_prime, S1, S0);
  and and_62 (and_62_out, C, S2);
  and and_63 (and_63_out, S3_prime, S1);
  and and_64 (and_64_out, C_prime, S2, S0);
  and and_65 (and_65_out, C_prime, S2_prime, S0_prime);
  and and_66 (and_66_out, C_prime, S3, S1_prime);
  and and_67 (and_67_out, C, S3_prime, S2_prime);
  and and_68 (and_68_out, C, S2, S0_prime);
  and and_69 (and_69_out, S3, S1_prime, S0);
  and and_70 (and_70_out, C, S2_prime, S1);
  or or_7 (G0, and_19_out, and_20_out, and_21_out, and_22_out, and_23_out, and_24_out, and_25_out);
  or or_8 (F0, and_26_out, and_27_out, and_28_out, and_29_out, and_30_out, and_31_out, and_32_out, and_33_out);
  or or_9 (E0, and_34_out, and_35_out, and_36_out, and_37_out, and_38_out);
  or or_10 (C0, S0, and_49_out, and_50_out, and_51_out, and_52_out, and_53_out);
  or or_11 (B0, and_54_out, and_55_out, and_56_out, and_57_out, and_58_out, and_59_out, and_60_out, and_61_out, and_62_out);
  or or_12 (D0, and_39_out, and_40_out, and_41_out, and_42_out, and_43_out, and_44_out, and_45_out, and_46_out, and_47_out, and_48_out);
  or or_13 (A0, and_63_out, and_64_out, and_65_out, and_66_out, and_67_out, and_68_out, and_69_out, and_70_out);

  assign B1 = 1'b1;
endmodule

module DUAL_7_SEGMENT_DECODER_WITH_BUILT_DECODER (
  input  C,
  input  S3,
  input  S2,
  input  S1,
  input  S0,
  output A1,
  output A0,
  output B1,
  output B0,
  output C1,
  output C0,
  output D1,
  output D0,
  output E1,
  output E0,
  output F1,
  output F0,
  output G1,
  output G0
);

  wire and_1_out, and_2_out, and_3_out, and_4_out, and_6_out, and_7_out, and_8_out, and_9_out, and_10_out,
       and_11_out, and_12_out, and_13_out, and_14_out, and_15_out, and_16_out, and_17_out, and_18_out,
       C_prime, or_1_out, or_3_out, or_4_out, or_5_out, S0_prime, S1_prime, S2_prime, S3_prime, xnor_1_out;
  wire [1:0] or_2_out;
  wire [3:1] or_8_out;

  not not_1 (C_prime, C);
  Pull_Resistor pull_resistor_1 (.node(C));
  not not_2 (S3_prime, S3);
  or or_1 (or_1_out, S2, S3);
  and and_1 (and_1_out, C_prime, S3, S1);
  and and_2 (and_2_out, C_prime, S3, S2);
  and and_3 (and_3_out, C, S3_prime, S2_prime);
  and and_4 (and_4_out, S3, S2, S1);
  not not_3 (S2_prime, S2);
  and and_5 (or_2_out[1], C, or_1_out);
  not not_4 (S1_prime, S1);
  or or_2 (or_2_out[0], and_1_out, and_2_out, and_3_out, and_4_out);
  not not_5 (S0_prime, S0);
  // DisplayDecoder displaydecoder_1: pin names not known; wires that end beside it: {2'b00, or_2_out}, A1, B1, C1, D1, E1, F1, G1
  and and_6 (and_6_out, S3_prime, S1);
  and and_7 (and_7_out, S3, S2, S1_prime);
  and and_8 (and_8_out, C, S2_prime);
  xnor xnor_1 (xnor_1_out, S3, S1);
  and and_9 (and_9_out, C_prime, S2);
  or or_3 (or_3_out, S3_prime, S1);
  and and_10 (and_10_out, C, S2_prime);
  or or_4 (or_4_out, S1_prime, S3);
  or or_5 (or_5_out, and_6_out, and_7_out);
  and and_11 (and_11_out, and_8_out, xnor_1_out);
  and and_12 (and_12_out, S3_prime, S2, S1);
  and and_13 (and_13_out, C_prime, S3, S2_prime, S1_prime);
  and and_14 (and_14_out, C, S3_prime, S2_prime, S1);
  and and_15 (and_15_out, C, S3, S2, S1_prime);
  and and_16 (and_16_out, and_9_out, or_3_out);
  and and_17 (and_17_out, and_10_out, or_4_out);
  and and_18 (and_18_out, C_prime, or_5_out);
  or or_6 (or_8_out[3], and_13_out, and_14_out, and_15_out);
  or or_7 (or_8_out[2], and_16_out, and_17_out);
  or or_8 (or_8_out[1], and_18_out, and_11_out, and_12_out);
  // DisplayDecoder displaydecoder_2: pin names not known; wires that end beside it: {or_8_out, S0}, A0, B0, C0, D0, E0, F0, G0

  // Notes on the sheet:
  //   7 segment decoder 1
  //   7 segment decoder 2
endmodule

module DUAL_7_SEGMENT_DECODER_WITH_BUILT_DECODER_REV_2 (
  input  C,
  input  S3,
  input  S2,
  input  S1,
  input  S0,
  output [6:0] Decoder_1,
  output [6:0] Decoder_0
);

  wire and_1_out, and_2_out, and_3_out, and_4_out, and_6_out, and_7_out, and_8_out, and_9_out, and_10_out,
       and_11_out, and_12_out, and_13_out, and_14_out, and_15_out, and_16_out, and_17_out, and_18_out,
       C_prime, or_1_out, or_3_out, or_4_out, or_5_out, S0_prime, S1_prime, S2_prime, S3_prime, xnor_1_out;
  wire [1:0] or_2_out;
  wire [3:1] or_8_out;

  not not_1 (C_prime, C);
  Pull_Resistor pull_resistor_1 (.node(C));
  not not_2 (S3_prime, S3);
  or or_1 (or_1_out, S2, S3);
  and and_1 (and_1_out, C_prime, S3, S1);
  and and_2 (and_2_out, C_prime, S3, S2);
  and and_3 (and_3_out, C, S3_prime, S2_prime);
  and and_4 (and_4_out, S3, S2, S1);
  not not_3 (S2_prime, S2);
  and and_5 (or_2_out[1], C, or_1_out);
  not not_4 (S1_prime, S1);
  or or_2 (or_2_out[0], and_1_out, and_2_out, and_3_out, and_4_out);
  not not_5 (S0_prime, S0);
  // DisplayDecoder displaydecoder_1: pin names not known; wires that end beside it: {2'b00, or_2_out}, Decoder_1[0], Decoder_1[1], Decoder_1[2], Decoder_1[3], Decoder_1[4], Decoder_1[5], Decoder_1[6]
  and and_6 (and_6_out, S3_prime, S1);
  and and_7 (and_7_out, S3, S2, S1_prime);
  and and_8 (and_8_out, C, S2_prime);
  xnor xnor_1 (xnor_1_out, S3, S1);
  and and_9 (and_9_out, C_prime, S2);
  or or_3 (or_3_out, S3_prime, S1);
  and and_10 (and_10_out, C, S2_prime);
  or or_4 (or_4_out, S1_prime, S3);
  or or_5 (or_5_out, and_6_out, and_7_out);
  and and_11 (and_11_out, and_8_out, xnor_1_out);
  and and_12 (and_12_out, S3_prime, S2, S1);
  and and_13 (and_13_out, C_prime, S3, S2_prime, S1_prime);
  and and_14 (and_14_out, C, S3_prime, S2_prime, S1);
  and and_15 (and_15_out, C, S3, S2, S1_prime);
  and and_16 (and_16_out, and_9_out, or_3_out);
  and and_17 (and_17_out, and_10_out, or_4_out);
  and and_18 (and_18_out, C_prime, or_5_out);
  or or_6 (or_8_out[3], and_13_out, and_14_out, and_15_out);
  or or_7 (or_8_out[2], and_16_out, and_17_out);
  or or_8 (or_8_out[1], and_18_out, and_11_out, and_12_out);
  // DisplayDecoder displaydecoder_2: pin names not known; wires that end beside it: {or_8_out, S0}, Decoder_0[0], Decoder_0[1], Decoder_0[2], Decoder_0[3], Decoder_0[4], Decoder_0[5], Decoder_0[6]

  // Notes on the sheet:
  //   7 segment decoder 1
  //   7 segment decoder 2
endmodule

module DUAL_7_SEGMENT_DECODER_WITHOUT_BUILT_DECODER (
  input  C,
  input  S3,
  input  S2,
  input  S1,
  input  S0,
  output [3:0] Decoder_1,
  output [3:0] Decoder_0
);

  wire and_1_out, and_2_out, and_3_out, and_4_out, and_6_out, and_7_out, and_8_out, and_9_out, and_10_out,
       and_11_out, and_12_out, and_13_out, and_14_out, and_15_out, and_16_out, and_17_out, and_18_out,
       C_prime, or_1_out, or_3_out, or_4_out, or_5_out, S0_prime, S1_prime, S2_prime, S3_prime, xnor_1_out;

  not not_1 (C_prime, C);
  Pull_Resistor pull_resistor_1 (.node(C));
  not not_2 (S3_prime, S3);
  or or_1 (or_1_out, S2, S3);
  and and_1 (and_1_out, C_prime, S3, S1);
  and and_2 (and_2_out, C_prime, S3, S2);
  and and_3 (and_3_out, C, S3_prime, S2_prime);
  and and_4 (and_4_out, S3, S2, S1);
  not not_3 (S2_prime, S2);
  and and_5 (Decoder_1[1], C, or_1_out);
  not not_4 (S1_prime, S1);
  or or_2 (Decoder_1[0], and_1_out, and_2_out, and_3_out, and_4_out);
  not not_5 (S0_prime, S0);
  and and_6 (and_6_out, S3_prime, S1);
  and and_7 (and_7_out, S3, S2, S1_prime);
  and and_8 (and_8_out, C, S2_prime);
  xnor xnor_1 (xnor_1_out, S3, S1);
  and and_9 (and_9_out, C_prime, S2);
  or or_3 (or_3_out, S3_prime, S1);
  and and_10 (and_10_out, C, S2_prime);
  or or_4 (or_4_out, S1_prime, S3);
  or or_5 (or_5_out, and_6_out, and_7_out);
  and and_11 (and_11_out, and_8_out, xnor_1_out);
  and and_12 (and_12_out, S3_prime, S2, S1);
  and and_13 (and_13_out, C_prime, S3, S2_prime, S1_prime);
  and and_14 (and_14_out, C, S3_prime, S2_prime, S1);
  and and_15 (and_15_out, C, S3, S2, S1_prime);
  and and_16 (and_16_out, and_9_out, or_3_out);
  and and_17 (and_17_out, and_10_out, or_4_out);
  and and_18 (and_18_out, C_prime, or_5_out);
  or or_6 (Decoder_0[3], and_13_out, and_14_out, and_15_out);
  or or_7 (Decoder_0[2], and_16_out, and_17_out);
  or or_8 (Decoder_0[1], and_18_out, and_11_out, and_12_out);

  assign Decoder_0[0] = S0;
  assign Decoder_1[3:2] = 2'b00;

  // Notes on the sheet:
  //   7 segment decoder 1
  //   7 segment decoder 2
endmodule

module decoder (
  input  in_1,
  input  [4:0] in_2,
  output [4:0] out_3
);

  wire clock_1_out;
  wire [6:0] dual_7_segment_decoder_with_built_decoder_rev_2_1_decoder_0,
       dual_7_segment_decoder_with_built_decoder_rev_2_1_decoder_1;

  Clock clock_1 (.out(clock_1_out));
  Counter #(.width(5), .max('h1f)) counter_1 (
    .load(in_1), .D(in_2), .Q(out_3), .clk(clock_1_out));  // open: count, carry, clr, preset, down
  _7_Segment_Display u_7_segment_display_1 (
    .g(dual_7_segment_decoder_with_built_decoder_rev_2_1_decoder_1[6]),
    .f(dual_7_segment_decoder_with_built_decoder_rev_2_1_decoder_1[5]),
    .a(dual_7_segment_decoder_with_built_decoder_rev_2_1_decoder_1[0]),
    .b(dual_7_segment_decoder_with_built_decoder_rev_2_1_decoder_1[1]),
    .e(dual_7_segment_decoder_with_built_decoder_rev_2_1_decoder_1[4]),
    .d(dual_7_segment_decoder_with_built_decoder_rev_2_1_decoder_1[3]),
    .c(dual_7_segment_decoder_with_built_decoder_rev_2_1_decoder_1[2]));  // open: dp
  DUAL_7_SEGMENT_DECODER_WITH_BUILT_DECODER_REV_2 dual_7_segment_decoder_with_built_decoder_rev_2_1 (
    .Decoder_1(dual_7_segment_decoder_with_built_decoder_rev_2_1_decoder_1),
    .Decoder_0(dual_7_segment_decoder_with_built_decoder_rev_2_1_decoder_0), .C(out_3[4]), .S3(out_3[3]),
    .S2(out_3[2]), .S1(out_3[1]), .S0(out_3[0]));
  _7_Segment_Display u_7_segment_display_2 (
    .g(dual_7_segment_decoder_with_built_decoder_rev_2_1_decoder_0[6]),
    .f(dual_7_segment_decoder_with_built_decoder_rev_2_1_decoder_0[5]),
    .a(dual_7_segment_decoder_with_built_decoder_rev_2_1_decoder_0[0]),
    .b(dual_7_segment_decoder_with_built_decoder_rev_2_1_decoder_0[1]),
    .e(dual_7_segment_decoder_with_built_decoder_rev_2_1_decoder_0[4]),
    .d(dual_7_segment_decoder_with_built_decoder_rev_2_1_decoder_0[3]),
    .c(dual_7_segment_decoder_with_built_decoder_rev_2_1_decoder_0[2]));  // open: dp
endmodule

module counter (
  output out_1,
  output out_2,
  output out_3,
  output out_4,
  output out_5
);

  wire clock_1_out;

  Clock clock_1 (.out(clock_1_out));
  J_K_Flip_Flop #(.trigger("falling")) j_k_ff_1 (
    .J(1'b1), .clk(clock_1_out), .K(1'b1), .Q(out_5));  // open: Qn, preset, reset
  J_K_Flip_Flop #(.trigger("falling")) j_k_ff_2 (
    .J(1'b1), .clk(out_5), .K(1'b1), .Q(out_4));  // open: Qn, preset, reset
  J_K_Flip_Flop #(.trigger("falling")) j_k_ff_3 (
    .J(1'b1), .clk(out_4), .K(1'b1), .Q(out_3));  // open: Qn, preset, reset
  J_K_Flip_Flop #(.trigger("falling")) j_k_ff_4 (
    .J(1'b1), .clk(out_3), .K(1'b1), .Q(out_2));  // open: Qn, preset, reset
  J_K_Flip_Flop #(.trigger("falling")) j_k_ff_5 (
    .J(1'b1), .clk(out_2), .K(1'b1), .Q(out_1));  // open: Qn, preset, reset
endmodule

module D___JK (
  input  CLK,
  input  J,
  input  K,
  output QN,
  output QN_prime
);

  wire and_1_out, and_2_out, not_1_out, or_1_out;

  not not_1 (not_1_out, K);
  and and_1 (and_1_out, QN, not_1_out);
  and and_2 (and_2_out, J, QN_prime);
  D_Flip_Flop #(.trigger("falling")) d_ff_1 (.clk(CLK), .D(or_1_out), .Q(QN), .Qn(QN_prime));  // open: preset, reset
  or or_1 (or_1_out, and_1_out, and_2_out);
endmodule

module COUNTER_USING_D_FLIP_FLOP (
  output out_1,
  output out_2,
  output out_3,
  output out_4,
  output out_5
);

  wire and_1_out, and_2_out, and_3_out, and_4_out, and_5_out, and_6_out, and_7_out, and_8_out, and_9_out,
       and_10_out, and_11_out, and_12_out, and_13_out, clock_1_out, d_ff_1_qn, d_ff_2_qn, d_ff_3_qn,
       d_ff_4_qn, d_ff_5_qn, d_ff_6_q, d_ff_6_qn, not_1_out, not_2_out, not_3_out, not_4_out, not_5_out,
       not_6_out, or_1_out, or_2_out, or_3_out, or_4_out, or_5_out, or_6_out, undriven;

  Clock clock_1 (.out(clock_1_out));
  not not_1 (not_1_out, 1'b1);
  and and_1 (and_1_out, out_5, not_1_out);
  and and_2 (and_2_out, 1'b1, d_ff_1_qn);
  or or_1 (or_1_out, and_1_out, and_2_out);
  and and_3 (and_3_out, 1'b1, undriven);
  D_Flip_Flop #(.trigger("falling")) d_ff_1 (
    .clk(clock_1_out), .D(or_1_out), .Q(out_5), .Qn(d_ff_1_qn), .reset(and_3_out));  // open: preset
  not not_2 (not_2_out, 1'b1);
  and and_4 (and_4_out, out_4, not_2_out);
  and and_5 (and_5_out, 1'b1, d_ff_2_qn);
  D_Flip_Flop #(.trigger("falling")) d_ff_2 (
    .clk(out_5), .D(or_2_out), .Q(out_4), .Qn(d_ff_2_qn), .reset(and_3_out));  // open: preset
  or or_2 (or_2_out, and_4_out, and_5_out);
  not not_3 (not_3_out, 1'b1);
  and and_6 (and_6_out, out_3, not_3_out);
  or or_3 (or_3_out, and_6_out, and_7_out);
  and and_7 (and_7_out, 1'b1, d_ff_3_qn);
  D_Flip_Flop #(.trigger("falling")) d_ff_3 (
    .clk(out_4), .D(or_3_out), .Q(out_3), .Qn(d_ff_3_qn), .reset(and_3_out));  // open: preset
  and and_8 (and_8_out, out_2, not_4_out);
  not not_4 (not_4_out, 1'b1);
  and and_9 (and_9_out, 1'b1, d_ff_4_qn);
  or or_4 (or_4_out, and_8_out, and_9_out);
  D_Flip_Flop #(.trigger("falling")) d_ff_4 (
    .clk(out_3), .D(or_4_out), .Q(out_2), .Qn(d_ff_4_qn), .reset(and_3_out));  // open: preset
  not not_5 (not_5_out, 1'b1);
  and and_10 (and_10_out, out_1, not_5_out);
  and and_11 (and_11_out, 1'b1, d_ff_5_qn);
  or or_5 (or_5_out, and_10_out, and_11_out);
  D_Flip_Flop #(.trigger("falling")) d_ff_5 (
    .clk(out_2), .D(or_5_out), .Q(out_1), .Qn(d_ff_5_qn), .reset(and_3_out));  // open: preset
  not not_6 (not_6_out, 1'b1);
  and and_12 (and_12_out, d_ff_6_q, not_6_out);
  and and_13 (and_13_out, 1'b1, d_ff_6_qn);
  D_Flip_Flop #(.trigger("falling")) d_ff_6 (
    .clk(out_1), .D(or_6_out), .Q(d_ff_6_q), .Qn(d_ff_6_qn), .reset(and_3_out));  // open: preset
  or or_6 (or_6_out, and_12_out, and_13_out);
endmodule

module D___T (
  input  CLK,
  input  T
);

  wire d_ff_1_q, xor_1_out;

  D_Flip_Flop d_ff_1 (.clk(CLK), .D(xor_1_out), .Q(d_ff_1_q));  // open: Qn, preset, reset
  xor xor_1 (xor_1_out, d_ff_1_q, T);
endmodule

module counter_with_max_selector_via_d_flip_flop (
  input  [1:0] MAX,
  input  CLK,
  output out_3,
  output out_4,
  output out_5,
  output out_6,
  output out_7
);

  wire _10_out, _20_out, _30_out, multiplexer_1_out, xor_1_out, xor_2_out, xor_3_out, xor_4_out, xor_5_out;

  Multiplexer #(.select(2), .enable("false")) multiplexer_1 (
    .in0(1'b0), .in1(_10_out), .in2(_20_out), .in3(_30_out), .out(multiplexer_1_out), .sel(MAX));
  and _10 (_10_out, out_6, out_7, out_4);
  and _20 (_20_out, out_5, out_7, out_3);
  and _30 (_30_out, out_3, out_4, out_5, out_6, out_7);
  xor xor_1 (xor_1_out, out_7, 1'b1);
  D_Flip_Flop #(.trigger("falling")) d_ff_1 (
    .clk(CLK), .D(xor_1_out), .Q(out_7), .reset(multiplexer_1_out));  // open: Qn, preset
  D_Flip_Flop #(.trigger("falling")) d_ff_2 (
    .clk(out_7), .D(xor_2_out), .Q(out_6), .reset(multiplexer_1_out));  // open: Qn, preset
  xor xor_2 (xor_2_out, out_6, 1'b1);
  xor xor_3 (xor_3_out, out_5, 1'b1);
  D_Flip_Flop #(.trigger("falling")) d_ff_3 (
    .clk(out_6), .D(xor_3_out), .Q(out_5), .reset(multiplexer_1_out));  // open: Qn, preset
  xor xor_4 (xor_4_out, out_4, 1'b1);
  D_Flip_Flop #(.trigger("falling")) d_ff_4 (
    .clk(out_5), .D(xor_4_out), .Q(out_4), .reset(multiplexer_1_out));  // open: Qn, preset
  xor xor_5 (xor_5_out, out_3, 1'b1);
  D_Flip_Flop #(.trigger("falling")) d_ff_5 (
    .clk(out_4), .D(xor_5_out), .Q(out_3), .reset(multiplexer_1_out));  // open: Qn, preset
endmodule

module counter_with_max_selector_5_10_15_20_25_30 (
  input  [2:0] MAX,
  input  CLK,
  output out_3,
  output out_4,
  output out_5,
  output out_6,
  output out_7
);

  wire bitselector_1_out, not_1_out, not_2_out, not_3_out, not_4_out, xor_1_out, xor_2_out, xor_3_out,
       xor_4_out, xor_5_out;
  wire [5:0] _5_out;

  BitSelector #(.width(6)) bitselector_1 (.in(_5_out), .out(bitselector_1_out), .sel(MAX));
  xor xor_1 (xor_1_out, out_7, 1'b1);
  and _5 (_5_out[0], out_6, out_5);
  and _10 (_5_out[1], out_6, out_7, out_4);
  not not_1 (not_1_out, out_4);
  not not_2 (not_2_out, out_5);
  and _15 (_5_out[2], out_3, not_1_out, not_2_out, not_3_out, not_4_out);
  not not_3 (not_3_out, out_6);
  not not_4 (not_4_out, out_7);
  and _20 (_5_out[3], out_5, out_7, out_3);
  and _25 (_5_out[4], out_3, out_4, out_6);
  and _30 (_5_out[5], out_3, out_4, out_5, out_6, out_7);
  D_Flip_Flop #(.trigger("falling")) d_ff_1 (
    .clk(CLK), .D(xor_1_out), .Q(out_7), .reset(bitselector_1_out));  // open: Qn, preset
  xor xor_2 (xor_2_out, out_6, 1'b1);
  D_Flip_Flop #(.trigger("falling")) d_ff_2 (
    .clk(out_7), .D(xor_2_out), .Q(out_6), .reset(bitselector_1_out));  // open: Qn, preset
  D_Flip_Flop #(.trigger("falling")) d_ff_3 (
    .clk(out_6), .D(xor_3_out), .Q(out_5), .reset(bitselector_1_out));  // open: Qn, preset
  xor xor_3 (xor_3_out, out_5, 1'b1);
  xor xor_4 (xor_4_out, out_4, 1'b1);
  D_Flip_Flop #(.trigger("falling")) d_ff_4 (
    .clk(out_5), .D(xor_4_out), .Q(out_4), .reset(bitselector_1_out));  // open: Qn, preset
  xor xor_5 (xor_5_out, out_3, 1'b1);
  D_Flip_Flop #(.trigger("falling")) d_ff_5 (
    .clk(out_4), .D(xor_5_out), .Q(out_3), .reset(bitselector_1_out));  // open: Qn, preset
endmodule

module COUNTER_TEST_30_SEC (
  input  [1:0] MAX_COUNT,
  input  [2:0] MAX_COUNT_2
);

  wire CLK_out, counter_with_max_selector_5_10_15_20_25_30_1_out_3,
       counter_with_max_selector_5_10_15_20_25_30_1_out_4,
       counter_with_max_selector_5_10_15_20_25_30_1_out_5,
       counter_with_max_selector_5_10_15_20_25_30_1_out_6,
       counter_with_max_selector_5_10_15_20_25_30_1_out_7, counter_with_max_selector_via_d_flip_flop_1_out_3,
       counter_with_max_selector_via_d_flip_flop_1_out_4, counter_with_max_selector_via_d_flip_flop_1_out_5,
       counter_with_max_selector_via_d_flip_flop_1_out_6, counter_with_max_selector_via_d_flip_flop_1_out_7;
  wire [6:0] dual_7_segment_decoder_with_built_decoder_rev_2_1_decoder_0,
       dual_7_segment_decoder_with_built_decoder_rev_2_1_decoder_1,
       dual_7_segment_decoder_with_built_decoder_rev_2_2_decoder_0,
       dual_7_segment_decoder_with_built_decoder_rev_2_2_decoder_1;

  Clock CLK (.out(CLK_out));
  counter_with_max_selector_via_d_flip_flop counter_with_max_selector_via_d_flip_flop_1 (
    .CLK(CLK_out), .MAX(MAX_COUNT), .out_3(counter_with_max_selector_via_d_flip_flop_1_out_3),
    .out_4(counter_with_max_selector_via_d_flip_flop_1_out_4),
    .out_5(counter_with_max_selector_via_d_flip_flop_1_out_5),
    .out_6(counter_with_max_selector_via_d_flip_flop_1_out_6),
    .out_7(counter_with_max_selector_via_d_flip_flop_1_out_7));
  DUAL_7_SEGMENT_DECODER_WITH_BUILT_DECODER_REV_2 dual_7_segment_decoder_with_built_decoder_rev_2_1 (
    .Decoder_1(dual_7_segment_decoder_with_built_decoder_rev_2_1_decoder_1),
    .Decoder_0(dual_7_segment_decoder_with_built_decoder_rev_2_1_decoder_0),
    .C(counter_with_max_selector_via_d_flip_flop_1_out_3),
    .S3(counter_with_max_selector_via_d_flip_flop_1_out_4),
    .S2(counter_with_max_selector_via_d_flip_flop_1_out_5),
    .S1(counter_with_max_selector_via_d_flip_flop_1_out_6),
    .S0(counter_with_max_selector_via_d_flip_flop_1_out_7));
  _7_Segment_Display u_7_segment_display_1 (
    .g(dual_7_segment_decoder_with_built_decoder_rev_2_1_decoder_1[6]),
    .f(dual_7_segment_decoder_with_built_decoder_rev_2_1_decoder_1[5]),
    .a(dual_7_segment_decoder_with_built_decoder_rev_2_1_decoder_1[0]),
    .b(dual_7_segment_decoder_with_built_decoder_rev_2_1_decoder_1[1]),
    .e(dual_7_segment_decoder_with_built_decoder_rev_2_1_decoder_1[4]),
    .d(dual_7_segment_decoder_with_built_decoder_rev_2_1_decoder_1[3]),
    .c(dual_7_segment_decoder_with_built_decoder_rev_2_1_decoder_1[2]));  // open: dp
  _7_Segment_Display u_7_segment_display_2 (
    .g(dual_7_segment_decoder_with_built_decoder_rev_2_1_decoder_0[6]),
    .f(dual_7_segment_decoder_with_built_decoder_rev_2_1_decoder_0[5]),
    .a(dual_7_segment_decoder_with_built_decoder_rev_2_1_decoder_0[0]),
    .b(dual_7_segment_decoder_with_built_decoder_rev_2_1_decoder_0[1]),
    .e(dual_7_segment_decoder_with_built_decoder_rev_2_1_decoder_0[4]),
    .d(dual_7_segment_decoder_with_built_decoder_rev_2_1_decoder_0[3]),
    .c(dual_7_segment_decoder_with_built_decoder_rev_2_1_decoder_0[2]));  // open: dp
  counter_with_max_selector_5_10_15_20_25_30 counter_with_max_selector_5_10_15_20_25_30_1 (
    .CLK(CLK_out), .out_3(counter_with_max_selector_5_10_15_20_25_30_1_out_3),
    .out_4(counter_with_max_selector_5_10_15_20_25_30_1_out_4),
    .out_5(counter_with_max_selector_5_10_15_20_25_30_1_out_5),
    .out_6(counter_with_max_selector_5_10_15_20_25_30_1_out_6),
    .out_7(counter_with_max_selector_5_10_15_20_25_30_1_out_7), .MAX(MAX_COUNT_2));
  DUAL_7_SEGMENT_DECODER_WITH_BUILT_DECODER_REV_2 dual_7_segment_decoder_with_built_decoder_rev_2_2 (
    .Decoder_1(dual_7_segment_decoder_with_built_decoder_rev_2_2_decoder_1),
    .Decoder_0(dual_7_segment_decoder_with_built_decoder_rev_2_2_decoder_0),
    .C(counter_with_max_selector_5_10_15_20_25_30_1_out_3),
    .S3(counter_with_max_selector_5_10_15_20_25_30_1_out_4),
    .S2(counter_with_max_selector_5_10_15_20_25_30_1_out_5),
    .S1(counter_with_max_selector_5_10_15_20_25_30_1_out_6),
    .S0(counter_with_max_selector_5_10_15_20_25_30_1_out_7));
  _7_Segment_Display u_7_segment_display_3 (
    .g(dual_7_segment_decoder_with_built_decoder_rev_2_2_decoder_1[6]),
    .f(dual_7_segment_decoder_with_built_decoder_rev_2_2_decoder_1[5]),
    .a(dual_7_segment_decoder_with_built_decoder_rev_2_2_decoder_1[0]),
    .b(dual_7_segment_decoder_with_built_decoder_rev_2_2_decoder_1[1]),
    .e(dual_7_segment_decoder_with_built_decoder_rev_2_2_decoder_1[4]),
    .d(dual_7_segment_decoder_with_built_decoder_rev_2_2_decoder_1[3]),
    .c(dual_7_segment_decoder_with_built_decoder_rev_2_2_decoder_1[2]));  // open: dp
  _7_Segment_Display u_7_segment_display_4 (
    .g(dual_7_segment_decoder_with_built_decoder_rev_2_2_decoder_0[6]),
    .f(dual_7_segment_decoder_with_built_decoder_rev_2_2_decoder_0[5]),
    .a(dual_7_segment_decoder_with_built_decoder_rev_2_2_decoder_0[0]),
    .b(dual_7_segment_decoder_with_built_decoder_rev_2_2_decoder_0[1]),
    .e(dual_7_segment_decoder_with_built_decoder_rev_2_2_decoder_0[4]),
    .d(dual_7_segment_decoder_with_built_decoder_rev_2_2_decoder_0[3]),
    .c(dual_7_segment_decoder_with_built_decoder_rev_2_2_decoder_0[2]));  // open: dp
endmodule

module saving_push_button_request (
  input  REQUEST_RESET,
  output out_2
);

  wire PUSH_TO_REQUEST_out, xor_1_out;

  Button PUSH_TO_REQUEST (.out(PUSH_TO_REQUEST_out));
  xor xor_1 (xor_1_out, REQUEST_RESET, PUSH_TO_REQUEST_out);
  D_Flip_Flop d_ff_1 (.clk(xor_1_out), .D(PUSH_TO_REQUEST_out), .Q(out_2));  // open: Qn, preset, reset

  // Notes on the sheet:
  //   WAIT UNTILL ALL 2 SIGNS IS RED AND READ THE PEDESTRIAN REQUEST
  //   IF REQUEST IS HIGH O TO WALK CYCLE AND RESET THE REQUEST TO LOW
endmodule
