// Logisim project Dual 7 Segment Decoder.circ as structural Verilog: 4 circuits, main circuit DUAL 7 SEGMENT DECODER DESIGN 1
module DUAL_7_SEGMENT_DECODER_DESIGN_1 (
  input  C,
  input  S3,
  input  S2,
  input  S1,
  input  S0,
  output G0,
  output G1,
  output F1,
  output E1,
  output F0,
  output D1,
  output C1,
  output B1,
  output A1,
  output E0,
  output D0,
  output C0,
  output B0,
  output A0
);

  wire and_1_out, and_2_out, and_3_out, and_4_out, and_5_out, and_6_out, and_7_out, and_8_out, and_9_out,
       and_10_out, and_11_out, and_12_out, and_13_out, and_14_out, and_15_out, and_16_out, and_17_out,
       and_18_out, and_19_out, and_20_out, and_21_out, and_22_out, and_23_out, and_24_out, and_25_out,
       and_26_out, and_27_out, and_28_out, and_29_out, and_30_out, and_31_out, and_32_out, and_33_out,
       and_34_out, and_35_out, and_36_out, and_37_out, and_38_out, and_39_out, and_40_out, and_41_out,
       and_42_out, and_43_out, and_44_out, and_45_out, and_46_out, and_47_out, and_48_out, and_49_out,
       and_50_out, and_51_out, and_52_out, and_53_out, and_54_out, and_55_out, and_56_out, and_57_out,
       and_58_out, and_59_out, and_60_out, and_61_out, and_62_out, and_63_out, and_64_out, and_65_out,
       and_66_out, and_67_out, and_68_out, and_69_out, and_70_out, C_prime, S0_prime, S1_prime, S2_prime,
       S3_prime;

  not not_1 (C_prime, C);
  Pull_Resistor pull_resistor_1 (.node(C));
  not not_2 (S3_prime, S3);
  not not_3 (S2_prime, S2);
  not not_4 (S1_prime, S1);
  and and_1 (and_1_out, C, S2);
  and and_2 (and_2_out, C, S3);
  and and_3 (and_3_out, C_prime, S3_prime);
  and and_4 (and_4_out, C_prime, S2_prime, S1_prime);
  and and_5 (and_5_out, S3_prime, S2);
  and and_6 (and_6_out, C, S3, S2_prime);
  and and_7 (and_7_out, C_prime, S2_prime, S1_prime);
  and and_8 (and_8_out, C, S2, S1_prime);
  and and_9 (and_9_out, C_prime, S3_prime);
  and and_10 (and_10_out, C, S3);
  and and_11 (and_11_out, C_prime, S2_prime, S1_prime);
  and and_12 (and_12_out, S3_prime, S2);
  and and_13 (and_13_out, S3_prime, S2_prime);
  and and_14 (and_14_out, S3, S2, S1);
  and and_15 (and_15_out, C_prime, S3_prime);
  and and_16 (and_16_out, C, S3);
  and and_17 (and_17_out, C_prime, S2_prime, S1_prime);
  and and_18 (and_18_out, S3_prime, S2);
  not not_5 (S0_prime, S0);
  or or_1 (G1, and_1_out, and_2_out);
  or or_2 (F1, and_3_out, and_4_out);
  or or_3 (E1, and_3_out, and_5_out, and_6_out, and_7_out, and_8_out);
  or or_4 (D1, and_9_out, and_10_out, and_11_out, and_12_out);
  or or_5 (C1, C_prime, and_13_out, and_14_out);
  or or_6 (A1, and_15_out, and_16_out, and_17_out, and_18_out);
  and and_19 (and_19_out, S3_prime, S2_prime, S1);
  and and_20 (and_20_out, C_prime, S2, S1_prime);
  and and_21 (and_21_out, S3, S1_prime);
  and and_22 (and_22_out, C_prime, S3, S2);
  and and_23 (and_23_out, C, S2_prime, S0_prime);
  and and_24 (and_24_out, C, S3_prime, S1);
  and and_25 (and_25_out, S3_prime, S1, S0_prime);
  and and_26 (and_26_out, C_prime, S3_prime, S2, S1_prime);
  and and_27 (and_27_out, S3, S2_prime, S1_prime);
  and and_28 (and_28_out, C_prime, S3, S2, S1);
  and and_29 (and_29_out, C, S3_prime, S2_prime, S1);
  and and_30 (and_30_out, C, S3, S1_prime);
  and and_31 (and_31_out, S3_prime, S1_prime, S0_prime);
  and and_32 (and_32_out, C_prime, S3_prime, S2, S0_prime);
  and and_33 (and_33_out, S3, S1, S0_prime);
  and and_34 (and_34_out, S3_prime, S1, S0_prime);
  and and_35 (and_35_out, C_prime, S2_prime, S0_prime);
  and and_36 (and_36_out, S3, S2, S1_prime, S0_prime);
  and and_37 (and_37_out, C, S3_prime, S0_prime);
  and and_38 (and_38_out, C, S1, S0_prime);
  and and_39 (and_39_out, C_prime, S3_prime, S2_prime, S1);
  and and_40 (and_40_out, C_prime, S2, S1_prime, S0);
  and and_41 (and_41_out, S3_prime, S1, S0_prime);
  and and_42 (and_42_out, C_prime, S3, S2, S0);
  and and_43 (and_43_out, C, S3_prime, S2, S1);
  and and_44 (and_44_out, C, S3, S2_prime, S1_prime, S0);
  and and_45 (and_45_out, C_prime, S2_prime, S0_prime);
  and and_46 (and_46_out, S3, S2, S1_prime, S0_prime);
  and and_47 (and_47_out, C, S3_prime, S0_prime);
  and and_48 (and_48_out, C, S1, S0_prime);
  and and_49 (and_49_out, C, S2_prime);
  and and_50 (and_50_out, S3_prime, S1_prime);
  and and_51 (and_51_out, C_prime, S2, S1);
  and and_52 (and_52_out, S3, S2_prime);
  and and_53 (and_53_out, C, S3);
  and and_54 (and_54_out, S3_prime, S1, S0);
  and and_55 (and_55_out, S3, S1_prime, S0_prime);
  and and_56 (and_56_out, C_prime, S1_prime, S0_prime);
  and and_57 (and_57_out, S3_prime, S2_prime, S0);
  and and_58 (and_58_out, S3_prime, S2_prime, S1);
  and and_59 (and_59_out, C_prime, S3, S1_prime);
  and and_60 (and_60_out, C_prime, S3, S0_prime);
  and and_61 (and_61_out, S2_prime, S1, S0);
  and and_62 (and_62_out, C, S2);
  and and_63 (and_63_out, S3_prime, S1);
  and and_64 (and_64_out, C_prime, S2, S0);
  and and_65 (and_65_out, C_prime, S2_prime, S0_prime);
  and and_66 (and_66_out, C_prime, S3, S1_prime);
  and and_67 (and_67_out, C, S3_prime, S2_prime);
  and and_68 (and_68_out, C, S2, S0_prime);
  and and_69 (and_69_out, S3, S1_prime, S0);
  and and_70 (and_70_out, C, S2_prime, S1);
  or or_7 (G0, and_19_out, and_20_out, and_21_out, and_22_out, and_23_out, and_24_out, and_25_out);
  or or_8 (F0, and_26_out, and_27_out, and_28_out, and_29_out, and_30_out, and_31_out, and_32_out, and_33_out);
  or or_9 (E0, and_34_out, and_35_out, and_36_out, and_37_out, and_38_out);
  or or_10 (C0, S0, and_49_out, and_50_out, and_51_out, and_52_out, and_53_out);
  or or_11 (B0, and_54_out, and_55_out, and_56_out, and_57_out, and_58_out, and_59_out, and_60_out, and_61_out, and_62_out);
  or or_12 (D0, and_39_out, and_40_out, and_41_out, and_42_out, and_43_out, and_44_out, and_45_out, and_46_out, and_47_out, and_48_out);
  or or_13 (A0, and_63_out, and_64_out, and_65_out, and_66_out, and_67_out, and_68_out, and_69_out, and_70_out);

  assign B1 = 1'b1;
endmodule

module DUAL_7_SEGMENT_DECODER_WITH_BUILT_DECODER (
  input  C,
  input  S3,
  input  S2,
  input  S1,
  input  S0,
  output A1,
  output A0,
  output B1,
  output B0,
  output C1,
  output C0,
  output D1,
  output D0,
  output E1,
  output E0,
  output F1,
  output F0,
  output G1,
  output G0
);

  wire and_1_out, and_2_out, and_3_out, and_4_out, and_6_out, and_7_out, and_8_out, and_9_out, and_10_out,
       and_11_out, and_12_out, and_13_out, and_14_out, and_15_out, and_16_out, and_17_out, and_18_out,
       C_prime, or_1_out, or_3_out, or_4_out, or_5_out, S0_prime, S1_prime, S2_prime, S3_prime, xnor_1_out;
  wire [1:0] or_2_out;
  wire [3:1] or_8_out;

  not not_1 (C_prime, C);
  Pull_Resistor pull_resistor_1 (.node(C));
  not not_2 (S3_prime, S3);
  or or_1 (or_1_out, S2, S3);
  and and_1 (and_1_out, C_prime, S3, S1);
  and and_2 (and_2_out, C_prime, S3, S2);
  and and_3 (and_3_out, C, S3_prime, S2_prime);
  and and_4 (and_4_out, S3, S2, S1);
  not not_3 (S2_prime, S2);
  and and_5 (or_2_out[1], C, or_1_out);
  not not_4 (S1_prime, S1);
  or or_2 (or_2_out[0], and_1_out, and_2_out, and_3_out, and_4_out);
  not not_5 (S0_prime, S0);
  // DisplayDecoder displaydecoder_1: pin names not known; wires that end beside it: {2'b00, or_2_out}, A1, B1, C1, D1, E1, F1, G1
  and and_6 (and_6_out, S3_prime, S1);
  and and_7 (and_7_out, S3, S2, S1_prime);
  and and_8 (and_8_out, C, S2_prime);
  xnor xnor_1 (xnor_1_out, S3, S1);
  and and_9 (and_9_out, C_prime, S2);
  or or_3 (or_3_out, S3_prime, S1);
  and and_10 (and_10_out, C, S2_prime);
  or or_4 (or_4_out, S1_prime, S3);
  or or_5 (or_5_out, and_6_out, and_7_out);
  and and_11 (and_11_out, and_8_out, xnor_1_out);
  and and_12 (and_12_out, S3_prime, S2, S1);
  and and_13 (and_13_out, C_prime, S3, S2_prime, S1_prime);
  and and_14 (and_14_out, C, S3_prime, S2_prime, S1);
  and and_15 (and_15_out, C, S3, S2, S1_prime);
  and and_16 (and_16_out, and_9_out, or_3_out);
  and and_17 (and_17_out, and_10_out, or_4_out);
  and and_18 (and_18_out, C_prime, or_5_out);
  or or_6 (or_8_out[3], and_13_out, and_14_out, and_15_out);
  or or_7 (or_8_out[2], and_16_out, and_17_out);
  or or_8 (or_8_out[1], and_18_out, and_11_out, and_12_out);
  // DisplayDecoder displaydecoder_2: pin names not known; wires that end beside it: {or_8_out, S0}, A0, B0, C0, D0, E0, F0, G0

  // Notes on the sheet:
  //   7 segment decoder 1
  //   7 segment decoder 2
endmodule

module DUAL_7_SEGMENT_DECODER_WITH_BUILT_DECODER_REV_2 (
  input  C,
  input  S3,
  input  S2,
  input  S1,
  input  S0,
  output [6:0] Decoder_1,
  output [6:0] Decoder_0
);

  wire and_1_out, and_2_out, and_3_out, and_4_out, and_6_out, and_7_out, and_8_out, and_9_out, and_10_out,
       and_11_out, and_12_out, and_13_out, and_14_out, and_15_out, and_16_out, and_17_out, and_18_out,
       C_prime, or_1_out, or_3_out, or_4_out, or_5_out, S0_prime, S1_prime, S2_prime, S3_prime, xnor_1_out;
  wire [1:0] or_2_out;
  wire [3:1] or_8_out;

  not not_1 (C_prime, C);
  Pull_Resistor pull_resistor_1 (.node(C));
  not not_2 (S3_prime, S3);
  or or_1 (or_1_out, S2, S3);
  and and_1 (and_1_out, C_prime, S3, S1);
  and and_2 (and_2_out, C_prime, S3, S2);
  and and_3 (and_3_out, C, S3_prime, S2_prime);
  and and_4 (and_4_out, S3, S2, S1);
  not not_3 (S2_prime, S2);
  and and_5 (or_2_out[1], C, or_1_out);
  not not_4 (S1_prime, S1);
  or or_2 (or_2_out[0], and_1_out, and_2_out, and_3_out, and_4_out);
  not not_5 (S0_prime, S0);
  // DisplayDecoder displaydecoder_1: pin names not known; wires that end beside it: {2'b00, or_2_out}, Decoder_1[0], Decoder_1[1], Decoder_1[2], Decoder_1[3], Decoder_1[4], Decoder_1[5], Decoder_1[6]
  and and_6 (and_6_out, S3_prime, S1);
  and and_7 (and_7_out, S3, S2, S1_prime);
  and and_8 (and_8_out, C, S2_prime);
  xnor xnor_1 (xnor_1_out, S3, S1);
  and and_9 (and_9_out, C_prime, S2);
  or or_3 (or_3_out, S3_prime, S1);
  and and_10 (and_10_out, C, S2_prime);
  or or_4 (or_4_out, S1_prime, S3);
  or or_5 (or_5_out, and_6_out, and_7_out);
  and and_11 (and_11_out, and_8_out, xnor_1_out);
  and and_12 (and_12_out, S3_prime, S2, S1);
  and and_13 (and_13_out, C_prime, S3, S2_prime, S1_prime);
  and and_14 (and_14_out, C, S3_prime, S2_prime, S1);
  and and_15 (and_15_out, C, S3, S2, S1_prime);
  and and_16 (and_16_out, and_9_out, or_3_out);
  and and_17 (and_17_out, and_10_out, or_4_out);
  and and_18 (and_18_out, C_prime, or_5_out);
  or or_6 (or_8_out[3], and_13_out, and_14_out, and_15_out);
  or or_7 (or_8_out[2], and_16_out, and_17_out);
  or or_8 (or_8_out[1], and_18_out, and_11_out, and_12_out);
  // DisplayDecoder displaydecoder_2: pin names not known; wires that end beside it: {or_8_out, S0}, Decoder_0[0], Decoder_0[1], Decoder_0[2], Decoder_0[3], Decoder_0[4], Decoder_0[5], Decoder_0[6]

  // Notes on the sheet:
  //   7 segment decoder 1
  //   7 segment decoder 2
endmodule

module DUAL_7_SEGMENT_DECODER_WITHOUT_BUILT_DECODER (
  input  C,
  input  S3,
  input  S2,
  input  S1,
  input  S0,
  output [3:0] Decoder_1,
  output [3:0] Decoder_0
);

  wire and_1_out, and_2_out, and_3_out, and_4_out, and_6_out, and_7_out, and_8_out, and_9_out, and_10_out,
       and_11_out, and_12_out, and_13_out, and_14_out, and_15_out, and_16_out, and_17_out, and_18_out,
       C_prime, or_1_out, or_3_out, or_4_out, or_5_out, S0_prime, S1_prime, S2_prime, S3_prime, xnor_1_out;

  not not_1 (C_prime, C);
  Pull_Resistor pull_resistor_1 (.node(C));
  not not_2 (S3_prime, S3);
  or or_1 (or_1_out, S2, S3);
  and and_1 (and_1_out, C_prime, S3, S1);
  and and_2 (and_2_out, C_prime, S3, S2);
  and and_3 (and_3_out, C, S3_prime, S2_prime);
  and and_4 (and_4_out, S3, S2, S1);
  not not_3 (S2_prime, S2);
  and and_5 (Decoder_1[1], C, or_1_out);
  not not_4 (S1_prime, S1);
  or or_2 (Decoder_1[0], and_1_out, and_2_out, and_3_out, and_4_out);
  not not_5 (S0_prime, S0);
  and and_6 (and_6_out, S3_prime, S1);
  and and_7 (and_7_out, S3, S2, S1_prime);
  and and_8 (and_8_out, C, S2_prime);
  xnor xnor_1 (xnor_1_out, S3, S1);
  and and_9 (and_9_out, C_prime, S2);
  or or_3 (or_3_out, S3_prime, S1);
  and and_10 (and_10_out, C, S2_prime);
  or or_4 (or_4_out, S1_prime, S3);
  or or_5 (or_5_out, and_6_out, and_7_out);
  and and_11 (and_11_out, and_8_out, xnor_1_out);
  and and_12 (and_12_out, S3_prime, S2, S1);
  and and_13 (and_13_out, C_prime, S3, S2_prime, S1_prime);
  and and_14 (and_14_out, C, S3_prime, S2_prime, S1);
  and and_15 (and_15_out, C, S3, S2, S1_prime);
  and and_16 (and_16_out, and_9_out, or_3_out);
  and and_17 (and_17_out, and_10_out, or_4_out);
  and and_18 (and_18_out, C_prime, or_5_out);
  or or_6 (Decoder_0[3], and_13_out, and_14_out, and_15_out);
  or or_7 (Decoder_0[2], and_16_out, and_17_out);
  or or_8 (Decoder_0[1], and_18_out, and_11_out, and_12_out);

  assign Decoder_0[0] = S0;
  assign Decoder_1[3:2] = 2'b00;

  // Notes on the sheet:
  //   7 segment decoder 1
  //   7 segment decoder 2
endmodule
